// Logisim project Calculator.circ as structural Verilog: 4 circuits, main circuit main
module main (
  input  in_1,
  input  in_2,
  input  in_3,
  input  in_4,
  input  in_5,
  input  in_6,
  input  in_7,
  input  in_8
);

  wire addition_1_out_7, addition_1_out_8, addition_1_out_9, addition_1_out_10, n7432_1_p2, n7448_1_p10,
       n7448_1_p11, n7448_1_p12, n7448_1_p13, n7448_1_p14, n7448_1_p15, n7448_1_p16, n74157_1_p3,
       n74157_1_p4, n74157_1_p8, n74157_1_p9, n74157_1_p10, n74157_2_p2, n74157_2_p4, n74157_2_p5,
       n74157_2_p7, n74157_2_p11, n74157_2_p13, n74157_2_p14, n74157_2_p16, n74157_3_p2, n74157_3_p4,
       n74157_3_p5, n74157_3_p13, n74157_4_p3, n74157_4_p4, n74157_4_p6, n74157_4_p7, n74157_4_p12,
       n74157_4_p13, n74157_4_p15, n74157_5_p2, n74157_5_p5, n74157_5_p11, n74157_5_p14, not_1_out,
       remainder_1_out_10, remainder_1_y, remainder_1_z, zero_flag_1_out_5;

  // _74157 74157_1: pin names not known; wires that end beside it: in_7, 1'b0, n74157_1_p3, n74157_1_p4, 1'b0, 1'b1, 1'b0, n74157_1_p8, n74157_1_p9, n74157_1_p10
  Remainder remainder_1 (
    .A(in_1), .B(in_2), .C(in_3), .D(in_4), .E(in_5), .F(in_6), .N(n74157_1_p9), .Y(remainder_1_y),
    .Z(remainder_1_z), .out_10(remainder_1_out_10));
  // _74157 74157_2: pin names not known; wires that end beside it: in_7, n74157_2_p2, remainder_1_z, n74157_2_p4, n74157_2_p5, remainder_1_y, n74157_2_p7, 1'b0, 1'b1, 1'b0, n74157_2_p11, 1'b0, n74157_2_p13, n74157_2_p14, 1'b0, n74157_2_p16
  // _74157 74157_3: pin names not known; wires that end beside it: in_8, n74157_3_p2, 1'b0, n74157_3_p4, n74157_3_p5, 1'b0, n74157_1_p8, 1'b0, 1'b1, 1'b0, 1'b0, n74157_3_p2, n74157_3_p13, remainder_1_out_10, 1'b0, n74157_1_p3
  Multiplier multiplier_1 (
    .A(in_1), .B(in_2), .C(in_3), .D(in_4), .E(in_5), .F(in_6), .N(n74157_3_p5), .W(n74157_2_p14),
    .X(n74157_2_p11), .Y(n74157_2_p5), .Z(n74157_2_p2));
  // _74157 74157_4: pin names not known; wires that end beside it: in_8, n74157_2_p4, n74157_4_p3, n74157_4_p4, n74157_2_p7, n74157_4_p6, n74157_4_p7, 1'b0, 1'b1, 1'b0, n74157_2_p13, n74157_4_p12, n74157_4_p13, n74157_2_p16, n74157_4_p15, n74157_3_p2
  // _7432 7432_1: pin names not known; wires that end beside it: 1'b0, n7432_1_p2, n74157_3_p13, n74157_1_p10, 1'b1
  addition addition_1 (
    .A(in_6), .B(in_5), .C(in_4), .D(in_3), .E(in_2), .F(in_1), .out_7(addition_1_out_7),
    .out_8(addition_1_out_8), .out_9(addition_1_out_9), .out_10(addition_1_out_10));
  // _74157 74157_5: pin names not known; wires that end beside it: in_7, n74157_5_p2, addition_1_out_7, n74157_4_p3, n74157_5_p5, addition_1_out_8, n74157_4_p6, 1'b0, 1'b1, 1'b0, n74157_5_p11, addition_1_out_9, n74157_4_p12, n74157_5_p14, addition_1_out_10, n74157_4_p15
  // _7448 7448_1: pin names not known; wires that end beside it: n74157_4_p7, n74157_4_p13, 1'b1, 1'b1, 1'b1, n74157_3_p4, n74157_4_p4, 1'b0, 1'b1, n7448_1_p10, n7448_1_p11, n7448_1_p12, n7448_1_p13, n7448_1_p14, n7448_1_p15, n7448_1_p16
  not not_1 (not_1_out, in_4);
  addition addition_2 (
    .A(in_6), .B(in_5), .C(not_1_out), .D(in_3), .E(in_2), .F(in_1), .out_7(n74157_5_p2),
    .out_8(n74157_5_p5), .out_9(n74157_5_p11), .out_10(n74157_5_p14));
  zero_flag zero_flag_1 (
    .in_1(n74157_4_p4), .in_2(n74157_4_p7), .in_3(n74157_4_p13), .in_4(n74157_3_p2), .out_5(zero_flag_1_out_5));
  _7_Segment_Display u_7_segment_display_1 (.g(n7432_1_p2));  // open: f, a, b, e, d, c, dp
  _7_Segment_Display u_7_segment_display_2 (
    .g(n7448_1_p11), .f(n7448_1_p10), .a(n7448_1_p12), .b(n7448_1_p13), .e(n7448_1_p16), .d(n7448_1_p15),
    .c(n7448_1_p14));  // open: dp
  LED led_1 (.in(zero_flag_1_out_5));
  LED led_2 (.in(n74157_1_p4));

  // Notes on the sheet:
  //   1
  //   0
  //   0
  //   1
  //   1
  //   0
  //   multiplication
  //   subtraction
  //   1
  //   remainder
  //   0
  //   addition
  //   ZERO FLAG
  //   DIVISION BY ZERO
endmodule

module Remainder (
  input  A,
  input  B,
  input  C,
  input  D,
  input  E,
  input  F,
  output N,
  output Y,
  output Z,
  output out_10
);

  wire n7404_1_p2, n7404_1_p9, n7404_1_p11, n7408_1_p3, n7408_1_p6, n7408_1_p8, n7408_1_p10, n7408_1_p11,
       n7408_1_p12, n7408_2_p9;

  // _7408 7408_1: pin names not known; wires that end beside it: 1'b0, Y, n7408_1_p3, n7408_1_p3, F, n7408_1_p6, E, n7408_1_p8, n7408_1_p6, n7408_1_p10, n7408_1_p11, n7408_1_p12, B, 1'b1
  // _7404 7404_1: pin names not known; wires that end beside it: 1'b0, n7404_1_p2, n7408_1_p8, n7408_1_p12, n7408_1_p11, Y, C, n7408_1_p10, n7404_1_p9, Z, n7404_1_p11, 1'b1
  // _7408 7408_2: pin names not known; wires that end beside it: 1'b0, N, n7404_1_p11, A, B, n7404_1_p2, F, Z, n7408_2_p9, n7404_1_p9, C, n7408_2_p9, D, E, 1'b1
  // _7402 7402_1: pin names not known; wires that end beside it: 1'b0, E, F, out_10, 1'b1
endmodule

module Multiplier (
  input  A,
  input  B,
  input  C,
  input  D,
  input  E,
  input  F,
  output N,
  output W,
  output X,
  output Y,
  output Z
);

  wire n7408_1_p3, n7408_1_p4, n7408_2_p3, n7408_2_p4, n7408_2_p5, n7408_2_p7, n7432_1_p3, n7432_1_p7;

  // _7408 7408_1: pin names not known; wires that end beside it: 1'b0, 1'b1, n7408_1_p3, n7408_1_p4, N
  // _7408 7408_2: pin names not known; wires that end beside it: 1'b0, 1'b1, n7408_2_p3, n7408_2_p4, n7408_2_p5, n7408_2_p5, n7408_2_p7, W
  // _7432 7432_1: pin names not known; wires that end beside it: 1'b0, n7408_1_p3, n7432_1_p3, W, X, n7432_1_p3, n7432_1_p7, n7432_1_p7, Y, Z, 1'b1
  // _7408 7408_3: pin names not known; wires that end beside it: 1'b1, B, C, E, E, n7408_2_p7, n7408_2_p3, B, C, F, F, n7408_2_p4, Z, 1'b0
  // _7486 7486_1: pin names not known; wires that end beside it: n7408_2_p3, n7408_2_p4, Y, n7408_2_p5, n7408_2_p7, X, 1'b0, 1'b1, A, D, n7408_1_p4
endmodule

module zero_flag (
  input  in_1,
  input  in_2,
  input  in_3,
  input  in_4,
  output out_5
);

  wire n7432_1_p2, n7432_1_p3, n7432_1_p7;

  // _7432 7432_1: pin names not known; wires that end beside it: 1'b0, n7432_1_p2, n7432_1_p3, in_4, in_3, n7432_1_p3, n7432_1_p7, n7432_1_p7, in_2, in_1, 1'b1
  not not_1 (out_5, n7432_1_p2);
endmodule
